# Fritzing sketch Schema (saved by Fritzing 0.7.12b)
breadboards: 1

parts:
  Arduino1 = Arduino
  RHT1 = Humidity and Temperature Sensor RHT03
  Composants1 = Real Time Clock Module - DS1307 RTC Breakout Board
  Composants2 = Barometric Pressure Sensor - BMP085 Breakout
  R7 = Photocell (LDR) [package=THT]
  R5 = Rotary Potentiometer (Small) [maximum_resistance=100kΩ]
  LCD1 = LCD screen
  Q1 = Basic FET P-Channel [package="TO220 [THT]"]
  Q2 = Basic FET P-Channel [package="TO220 [THT]"]
  Q3 = Basic FET P-Channel [package="TO220 [THT]"]
  R9 = Resistor [tolerance=±5% resistance=220 package=THT]
  R10 = Resistor [tolerance=±5% resistance=220 package=THT]
  R11 = Resistor [tolerance=±5% resistance=220 package=THT]
  R4 = Resistor [tolerance=±5% resistance=10k package=THT]
  R8 = Resistor [tolerance=±5% resistance=10k package=THT]
  R6 = Resistor [tolerance=±5% resistance=220 package=THT]
  S1 = Toggle Switch [package=THT]  # not connected
  S2 = Toggle Switch [package=THT]  # not connected

nets (from the breadboard view):
  GND: Arduino1.GND, RHT1.GND_2, Composants1.GND, Composants2.SDA, R5.leg2, LCD1.VSS, LCD1.R/W, LCD1.LED-, Q1.source, Q2.source, Q3.source, R9.Pin_1, R10.Pin_1, R11.Pin_1, R8.Pin_1
  N1: Arduino1.D12, LCD1.DB7
  N2: Arduino1.D11, LCD1.DB6
  N3: Arduino1.D10, LCD1.DB5
  N4: Arduino1.D9, LCD1.DB4
  N5: Arduino1.D8, LCD1.E
  N6: Arduino1.D7, LCD1.RS
  N7: Arduino1.D6, Q1.gate
  N8: Arduino1.D5, Q2.gate
  N9: Arduino1.D3, Q3.gate
  N10: Arduino1.D2, RHT1.Data-signal, R4.Pin_1
  +5V: Arduino1.+5V, RHT1.Vcc, Composants1.5V, Composants2.SCL, R7.pin_1, R5.leg1, LCD1.VDD, R4.Pin_0, R6.Pin_1
  N11: Arduino1.A0, R7.pin_0, R8.Pin_0
  N12: Arduino1.A4, Composants1.SDA, Composants2.XCLR
  N13: Arduino1.A5, Composants1.SCL, Composants2.EOC
  N14: R5.wiper, LCD1.V0
  N15: Q1.drain, R9.Pin_0
  N16: Q2.drain, R10.Pin_0
  N17: Q3.drain, R11.Pin_0

notes:
  BMP085 3.3/5v
  3V3/EOC/CLR/
  SCL/SDA/5V/GND
  10 kΩ
  DS1307 RTC
  5v
  220 Ω
  DHT22
  R
  Sur Ruban
  LED
  G
  Sur Ruban
  LED
  10
  kΩ
  B
  Sur Ruban
  LED
  12V
  Sur Ruban
  LED
  Alimentation 12 V
  L'ampérage dépend du nombre de LED que vous branchez
  MOFSET IRFZ44 TO-220
  N-Channel 49A 55V
  Photorésistance
